// Logisim project cpu.circ as structural Verilog: 2 circuits, main circuit main
module main (
  input  [31:0] INSTRUCTION,
  input  CLOCK,
  output [31:0] FETCH_ADDRESS,
  output [31:0] s0_Value,
  output [31:0] s1_Value,
  output [31:0] s2_Value,
  output [31:0] ra_Value,
  output [31:0] sp_Value
);

  wire ALUsrc, and_1_out, and_2_out, and_3_out, branch, branched, comparator_1_eq, comparator_2_eq,
       comparator_3_eq, comparator_4_eq, comparator_5_eq, equal, ExtOp, isjal, jump, lui_select, main_1_p7,
       main_1_p11, main_1_p18, main_2_p6, main_3_p1, memToReg, MemWrite, nop, not_1_out, or_3_out, overflow,
       RegDst, RegWrite, shift_select;
  wire [3:0] aluop;
  wire [4:0] multiplexer_3_out, multiplexer_5_out;
  wire [5:0] funcode, opcode;
  wire [15:6] imm;
  wire [25:16] pip1;
  wire [27:0] shifter_2_out;
  wire [31:0] adder_3_out, aluResult, bit_extender_1_out, bit_extender_2_out, bit_extender_3_out, execPC_4,
       immresult, isbranch, isjump, memResult, multiplexer_1_out, multiplexer_4_out, multiplexer_7_out,
       multiplexer_8_out, multiplexer_9_out, multiplexer_11_out, multiplexer_12_out, PC_4, register_1_q,
       shifter_1_out, writeData, x, y;

  ControlUnit controlunit_1 (
    .opcode(opcode), .funcode(funcode), .Regdst(RegDst), .Alusrc(ALUsrc), .Memtoreg(memToReg),
    .RegWrite(RegWrite), .MemWrite(MemWrite), .ExtOP(ExtOp), .ALUop(aluop), .isjal(isjal), .jump(jump),
    .branch(branch), .luiselect(lui_select), .shift_select(shift_select));
  Multiplexer #(.width(32)) multiplexer_1 (.in0(PC_4), .in1(isjump), .out(multiplexer_1_out), .sel(nop));  // open: en
  Register #(.width(32)) register_1 (.D(FETCH_ADDRESS), .Q(register_1_q), .clk(CLOCK));  // open: en, clr
  Shifter #(.width(32)) shifter_1 (.in(immresult), .\dist (5'b00010), .out(shifter_1_out));
  Comparator #(.width(6)) comparator_1 (.a(opcode), .b(6'b000100), .eq(comparator_1_eq));  // open: gt, lt
  Comparator #(.width(6)) comparator_2 (.a(opcode), .b(6'b000101), .eq(comparator_2_eq));  // open: gt, lt
  Comparator #(.width(6)) comparator_3 (.a(opcode), .b(6'b000110), .eq(comparator_3_eq));  // open: gt, lt
  Register #(.width(32)) PC (.D(multiplexer_1_out), .Q(FETCH_ADDRESS), .clk(CLOCK));  // open: en, clr
  not not_1 (not_1_out, equal);
  Adder #(.width(32)) adder_1 (.a(FETCH_ADDRESS), .b(32'h4), .out(PC_4));  // open: cin, cout
  Adder #(.width(32)) adder_2 (.a(register_1_q), .b(32'h4), .out(execPC_4));  // open: cin, cout
  Adder #(.width(32)) adder_3 (.a(execPC_4), .b(shifter_1_out), .out(adder_3_out));  // open: cin, cout
  and and_1 (and_1_out, branch, comparator_1_eq, equal);
  and and_2 (and_2_out, branch, comparator_2_eq, not_1_out);
  and and_3 (and_3_out, branch, comparator_3_eq, overflow);
  Multiplexer #(.width(32)) multiplexer_2 (
    .in0(register_1_q), .in1(adder_3_out), .out(isbranch), .sel(branched));  // open: en
  or or_1 (branched, and_1_out, and_2_out, and_3_out);
  and and_4 (isjal, jump, RegWrite);
  Multiplexer #(.width(5)) multiplexer_3 (
    .in0(pip1[20:16]), .in1(imm[15:11]), .out(multiplexer_3_out), .sel(RegDst));  // open: en
  assign bit_extender_1_out = {{16{1'b0}}, {imm, funcode}};  // Bit_Extender bit_extender_1
  assign bit_extender_2_out = {{16{imm[15]}}, {imm, funcode}};  // Bit_Extender bit_extender_2
  Shifter #(.width(28)) shifter_2 (.in(INSTRUCTION[27:0]), .\dist (5'b00010), .out(shifter_2_out));
  Comparator #(.width(6)) comparator_4 (.a(opcode), .b(6'b000010), .eq(comparator_4_eq));  // open: gt, lt
  Comparator #(.width(6)) comparator_5 (.a(opcode), .b(6'b000011), .eq(comparator_5_eq));  // open: gt, lt
  Multiplexer #(.width(32)) multiplexer_4 (
    .in0(INSTRUCTION), .in1({32{1'b0}}), .out(multiplexer_4_out), .sel(nop));  // open: en
  Register #(.width(32)) register_2 (
    .D(multiplexer_4_out), .Q({opcode, pip1, imm, funcode}), .clk(CLOCK));  // open: en, clr
  assign bit_extender_3_out = {{27{1'b0}}, imm[10:6]};  // Bit_Extender bit_extender_3
  Multiplexer #(.width(5)) multiplexer_5 (
    .in0(multiplexer_3_out), .in1({5{1'b1}}), .out(multiplexer_5_out), .sel(isjal));  // open: en
  Multiplexer #(.width(32)) multiplexer_6 (
    .in0(bit_extender_1_out), .in1(bit_extender_2_out), .out(immresult), .sel(ExtOp));  // open: en
  buf or_2 (nop, 1'b0);  // OR_Gate
  Multiplexer #(.width(32)) multiplexer_7 (
    .in0(x), .in1({execPC_4[31:28], shifter_2_out}), .out(multiplexer_7_out), .sel(or_3_out));  // open: en
  or or_3 (or_3_out, comparator_4_eq, comparator_5_eq);
  Multiplexer #(.width(32)) multiplexer_8 (
    .in0(x), .in1(bit_extender_3_out), .out(multiplexer_8_out), .sel(shift_select));  // open: en
  Multiplexer #(.width(32)) multiplexer_9 (
    .in0(writeData), .in1(execPC_4), .out(multiplexer_9_out), .sel(isjal));  // open: en
  Multiplexer #(.width(32)) multiplexer_10 (
    .in0(isbranch), .in1(multiplexer_7_out), .out(isjump), .sel(jump));  // open: en
  // regfile_main main_1: pin names not known; wires that end beside it: branched, pip1[25:21], pip1[20:16], multiplexer_5_out, s0_Value, multiplexer_9_out, main_1_p7, s1_Value, RegWrite, s2_Value, main_1_p11, CLOCK, ra_Value, sp_Value, x, y, main_1_p11, main_1_p18
  Multiplexer #(.width(32)) multiplexer_11 (
    .in0(multiplexer_8_out), .in1(32'h10), .out(multiplexer_11_out), .sel(lui_select));  // open: en
  Multiplexer #(.width(32)) multiplexer_12 (
    .in0(y), .in1(immresult), .out(multiplexer_12_out), .sel(ALUsrc));  // open: en
  LED led_1 (.in(overflow));
  // alu_main main_2: pin names not known; wires that end beside it: main_1_p18, multiplexer_11_out, multiplexer_12_out, overflow, aluop, main_2_p6, equal, aluResult, main_2_p6
  // mem_main main_3: pin names not known; wires that end beside it: main_3_p1, aluResult, y, MemWrite, main_3_p1, CLOCK, main_1_p7, memResult
  Multiplexer #(.width(32)) multiplexer_13 (
    .in0(aluResult), .in1(memResult), .out(writeData), .sel(memToReg));  // open: en

  // Other names for the same wires on the sheet: clk = CLOCK; fetch_addr[31:0] = FETCH_ADDRESS; imm[5:0] = funcode;
  //   pip1 (some bits) = {opcode, imm, funcode}; shamt[4:0] = imm[10:6]; rd[4:0] = imm[15:11]; rt[4:0] = pip1[20:16];
  //   rs[4:0] = pip1[25:21]; ra[31:0] = ra_Value; s0[31:0] = s0_Value; s1[31:0] = s1_Value; s2[31:0] = s2_Value;
  //   sp[31:0] = sp_Value

  // Notes on the sheet:
  //   Output
  //   These are outputs/inputs from run.circ
  //   Inputs
  //   These are DEBUG/TEST outputs from your circuit.
endmodule

// Control Unit
module ControlUnit (
  input  [5:0] opcode,
  input  [5:0] funcode,
  output isjal,
  output jump,
  output branch,
  output luiselect,
  output shift_select,
  output Regdst,
  output Memtoreg,
  output Alusrc,
  output RegWrite,
  output MemWrite,
  output ExtOP,
  output [3:0] ALUop
);

  wire add, addi, addiu, addu, \and , andi, beq, bne, bov, comparator_1_eq, comparator_2_eq, comparator_3_eq,
       comparator_4_eq, comparator_5_eq, comparator_6_eq, comparator_7_eq, comparator_8_eq, comparator_9_eq,
       comparator_10_eq, comparator_11_eq, comparator_12_eq, comparator_13_eq, j, jal, jalr, jr, lui, lw,
       nop0, nop1, nop2, nop3, nop4, nop5, \or , ori, rtype, sll, slt, slti, sltiu, sltu, sra, srl, sub,
       subu, sw;

  not not_1 (nop5, opcode[5]);
  Comparator #(.width(6)) comparator_1 (.a(funcode), .b({6{1'b0}}), .eq(comparator_1_eq));  // open: gt, lt
  Comparator #(.width(6)) comparator_2 (.a(funcode), .b(6'b000010), .eq(comparator_2_eq));  // open: gt, lt
  Comparator #(.width(6), .mode("unsigned")) comparator_3 (
    .a(funcode), .b(6'b000011), .eq(comparator_3_eq));  // open: gt, lt
  Comparator #(.width(6), .mode("unsigned")) comparator_4 (
    .a(funcode), .b(6'b001000), .eq(comparator_4_eq));  // open: gt, lt
  Comparator #(.width(6), .mode("unsigned")) comparator_5 (
    .a(funcode), .b(6'b001001), .eq(comparator_5_eq));  // open: gt, lt
  Comparator #(.width(6), .mode("unsigned")) comparator_6 (
    .a(funcode), .b(6'b100000), .eq(comparator_6_eq));  // open: gt, lt
  Comparator #(.width(6), .mode("unsigned")) comparator_7 (
    .a(funcode), .b(6'b100001), .eq(comparator_7_eq));  // open: gt, lt
  Comparator #(.width(6), .mode("unsigned")) comparator_8 (
    .a(funcode), .b(6'b100010), .eq(comparator_8_eq));  // open: gt, lt
  Comparator #(.width(6), .mode("unsigned")) comparator_9 (
    .a(funcode), .b(6'b100011), .eq(comparator_9_eq));  // open: gt, lt
  Comparator #(.width(6), .mode("unsigned")) comparator_10 (
    .a(funcode), .b(6'b100100), .eq(comparator_10_eq));  // open: gt, lt
  Comparator #(.width(6), .mode("unsigned")) comparator_11 (
    .a(funcode), .b(6'b100101), .eq(comparator_11_eq));  // open: gt, lt
  Comparator #(.width(6), .mode("unsigned")) comparator_12 (
    .a(funcode), .b(6'b101010), .eq(comparator_12_eq));  // open: gt, lt
  Comparator #(.width(6), .mode("unsigned")) comparator_13 (
    .a(funcode), .b(6'b101011), .eq(comparator_13_eq));  // open: gt, lt
  not not_2 (nop4, opcode[4]);
  not not_3 (nop3, opcode[3]);
  and u_sll (sll, rtype, comparator_1_eq);
  and u_srl (srl, rtype, comparator_2_eq);
  and u_sra (sra, rtype, comparator_3_eq);
  and u_jr (jr, rtype, comparator_4_eq);
  and u_jalr (jalr, rtype, comparator_5_eq);
  and u_add (add, rtype, comparator_6_eq);
  and u_addu (addu, rtype, comparator_7_eq);
  and u_sub (sub, rtype, comparator_8_eq);
  and u_subu (subu, rtype, comparator_9_eq);
  and u_and (\and , rtype, comparator_10_eq);
  and u_or (\or , rtype, comparator_11_eq);
  and u_slt (slt, rtype, comparator_12_eq);
  and u_sltu (sltu, rtype, comparator_13_eq);
  not not_4 (nop2, opcode[2]);
  not not_5 (nop1, opcode[1]);
  not not_6 (nop0, opcode[0]);
  and u_sltiu (sltiu, opcode[0], opcode[1], nop2, opcode[3], nop4, nop5);
  and u_bov (bov, nop0, opcode[1], opcode[2], nop3, nop4, nop5);
  and u_Rtype (rtype, nop0, nop1, nop2, nop3, nop4, nop5);
  and u_addi (addi, nop0, nop1, nop2, opcode[3], nop4, nop5);
  and u_addiu (addiu, opcode[0], nop1, nop2, opcode[3], nop4, nop5);
  and u_slti (slti, nop0, opcode[1], nop2, opcode[3], nop4, nop5);
  and u_andi (andi, nop0, nop1, opcode[2], opcode[3], nop4, nop5);
  and u_ori (ori, opcode[0], nop1, opcode[2], opcode[3], nop4, nop5);
  and u_lui (lui, opcode[0], opcode[1], opcode[2], opcode[3], nop4, nop5);
  and u_lw (lw, opcode[0], opcode[1], nop2, nop3, nop4, opcode[5]);
  and u_sw (sw, opcode[0], opcode[1], nop2, opcode[3], nop4, opcode[5]);
  and u_j (j, nop0, opcode[1], nop2, nop3, nop4, nop5);
  and u_jal (jal, opcode[0], opcode[1], nop2, nop3, nop4, nop5);
  and u_beq (beq, nop0, nop1, opcode[2], nop3, nop4, nop5);
  and u_bne (bne, opcode[0], nop1, opcode[2], nop3, nop4, nop5);
  or u_Regdst (Regdst, rtype, 1'b0);
  or u_Alusrc (Alusrc, addiu, addi, andi, lui, lw, ori, slti, sltiu, sw);
  or u_Memtoreg (Memtoreg, lw, 1'b0);
  or u_Regwrite (RegWrite, add, addi, addiu, addu, \and , andi, jal, jalr, lui, lw, \or , ori, slt, slti, sltiu, sltu, sll, sra, srl, sub, subu);
  or MemtWrite (MemWrite, sw, 1'b0);
  or u_ExtOP (ExtOP, beq, addi, addiu, lw, bov, slti, sltiu, sw, bne);
  or s3 (ALUop[3], \and , andi, \or , ori, slt, slti, sltiu, sltu, subu);
  or s2 (ALUop[2], add, addi, addiu, addu, lw, sltiu, sltu, sw, sub);
  or s1 (ALUop[1], addiu, addu, \or , ori, slt, slti, srl, sub);
  or s0 (ALUop[0], sub, sw, sra, slti, slt, lw, andi, \and , addi, add);
  or jalr_2 (isjal, jalr, jal);
  or u_jump (jump, jalr, jr, jal, j);
  or u_branch (branch, bov, bne, beq);
  or u_luiselect (luiselect, lui, 1'b0);
  or shift (shift_select, sll, srl, sra);

  // Other names for the same wires on the sheet: op0 = opcode[0]; op1 = opcode[1]; op2 = opcode[2]; op3 = opcode[3];
  //   op4 = opcode[4]; op5 = opcode[5]
endmodule
